// Logisim project juan_v2.circ as structural Verilog
module main (
);

  wire D_A, Flags_out_6, Flags_out_7, Flags_out_8, Flags_out_9, I_O, IO_e, IO_s, key_adapter_1_out_8,
       key_adapter_1_out_9, or_1_out, screen_1_out_6, screen_1_out_7, speaker_1_out_6, speaker_1_out_7,
       uc1_1_init, uc1_1_ir_set, uc1_1_t0_iar_s, uc1_1_to_acc_e, uc1_1_to_acc_s, uc1_1_to_bus1,
       uc1_1_to_flags_s, uc1_1_to_iar_e, uc1_1_to_mar_s, uc1_1_to_r0_e, uc1_1_to_r0_s, uc1_1_to_r1_e,
       uc1_1_to_r1_s, uc1_1_to_r2_e, uc1_1_to_r2_s, uc1_1_to_r3_e, uc1_1_to_r3_s, uc1_1_to_ram_e,
       uc1_1_to_ram_s, uc1_1_to_tmp_s, ula_1_a_lager, ula_1_c_out, ula_1_equal, ula_1_zero;
  wire [2:0] uc1_1_ula_op;
  wire [6:0] keyboard_1_data, screen_1_out_5;
  wire [7:0] acc_q, bus_1_out_3, controlled_buffer_1_out, IAR_q, IR_q, MAR_q, R0_q, R1_q, R2_q, R3_q, tmp_q,
       ula_1_out_7;
  wire [13:0] speaker_1_out_5;

  Register tmp (.D(controlled_buffer_1_out), .Q(tmp_q), .clk(uc1_1_to_tmp_s));  // open: en, clr
  ULA ula_1 (
    .A(controlled_buffer_1_out), .B(bus_1_out_3), .out_7(ula_1_out_7), .in_1(uc1_1_ula_op),
    .b_1(uc1_1_to_bus1), .c_in(Flags_out_6), .c_out(ula_1_c_out), .a_lager(ula_1_a_lager),
    .equal(ula_1_equal), .zero(ula_1_zero));
  // Probe on controlled_buffer_1_out
  bus1 bus_1 (.in_1(tmp_q), .out_3(bus_1_out_3), .in_2(uc1_1_to_bus1));
  Register acc (.D(ula_1_out_7), .Q(acc_q), .clk(uc1_1_to_acc_s));  // open: en, clr
  assign controlled_buffer_1_out = uc1_1_to_acc_e ? acc_q : 8'bz;  // Controlled_Buffer controlled_buffer_1
  flag Flags (
    .in_1(ula_1_c_out), .in_2(ula_1_a_lager), .in_3(ula_1_equal), .in_5(ula_1_zero), .in_4(uc1_1_to_flags_s),
    .out_6(Flags_out_6), .out_7(Flags_out_7), .out_8(Flags_out_8), .out_9(Flags_out_9));
  Keyboard keyboard_1 (
    .clk(key_adapter_1_out_8), .re(key_adapter_1_out_9), .data(keyboard_1_data));  // open: clr, avail
  key_adapter key_adapter_1 (
    .in_2(IO_e), .in_3(keyboard_1_data), .in_4(IO_s), .in_5(D_A), .in_6(I_O), .in_1(controlled_buffer_1_out),
    .out_7(controlled_buffer_1_out), .out_8(key_adapter_1_out_8), .out_9(key_adapter_1_out_9));
  assign controlled_buffer_1_out = uc1_1_to_r0_e ? R0_q : 8'bz;  // Controlled_Buffer controlled_buffer_2
  Register R0 (.D(controlled_buffer_1_out), .Q(R0_q), .clk(uc1_1_to_r0_s));  // open: en, clr
  assign controlled_buffer_1_out = uc1_1_to_r1_e ? R1_q : 8'bz;  // Controlled_Buffer controlled_buffer_3
  Register R1 (.D(controlled_buffer_1_out), .Q(R1_q), .clk(uc1_1_to_r1_s));  // open: en, clr
  Register IAR (.D(controlled_buffer_1_out), .Q(IAR_q), .clk(uc1_1_t0_iar_s));  // open: en, clr
  assign controlled_buffer_1_out = uc1_1_to_iar_e ? IAR_q : 8'bz;  // Controlled_Buffer controlled_buffer_4
  assign controlled_buffer_1_out = uc1_1_to_r2_e ? R2_q : 8'bz;  // Controlled_Buffer controlled_buffer_5
  Register R2 (.D(controlled_buffer_1_out), .Q(R2_q), .clk(uc1_1_to_r2_s));  // open: en, clr
  UC1 uc1_1 (
    .ULA_op(uc1_1_ula_op), .from_carry_out(Flags_out_6), .from_larger(Flags_out_7), .from_equal(Flags_out_8),
    .from_zero(Flags_out_9), .to_Flags_s(uc1_1_to_flags_s), .to_bus1(uc1_1_to_bus1),
    .to_TMP_s(uc1_1_to_tmp_s), .to_R0_s(uc1_1_to_r0_s), .to_R0_e(uc1_1_to_r0_e), .to_R1_s(uc1_1_to_r1_s),
    .to_R1_e(uc1_1_to_r1_e), .to_R2_s(uc1_1_to_r2_s), .to_R2_e(uc1_1_to_r2_e), .to_R3_s(uc1_1_to_r3_s),
    .to_R3_e(uc1_1_to_r3_e), .to_MAR_s(uc1_1_to_mar_s), .to_ACC_s(uc1_1_to_acc_s), .to_ACC_e(uc1_1_to_acc_e),
    .t0_IAR_s(uc1_1_t0_iar_s), .to_IAR_e(uc1_1_to_iar_e), .IR_input(IR_q), .IR_set(uc1_1_ir_set),
    .Input_Output(I_O), .Data_Address(D_A), .to_IO_e(IO_e), .to_IO_s(IO_s), .to_RAM_s(uc1_1_to_ram_s),
    .to_RAM_e(uc1_1_to_ram_e), .init(uc1_1_init));
  Register IR (.D(controlled_buffer_1_out), .Q(IR_q), .clk(uc1_1_ir_set));  // open: en, clr
  assign controlled_buffer_1_out = uc1_1_to_r3_e ? R3_q : 8'bz;  // Controlled_Buffer controlled_buffer_6
  Register R3 (.D(controlled_buffer_1_out), .Q(R3_q), .clk(uc1_1_to_r3_s));  // open: en, clr
  LED led_1 (.in(uc1_1_init));
  screen screen_1 (
    .in_2(IO_s), .in_3(D_A), .in_4(I_O), .in_1(controlled_buffer_1_out), .out_5(screen_1_out_5),
    .out_6(screen_1_out_6), .out_7(screen_1_out_7));
  or or_1 (or_1_out, uc1_1_to_ram_s, uc1_1_to_ram_e);
  TTY tty_1 (.data(screen_1_out_5), .clk(screen_1_out_6), .we(screen_1_out_7));  // open: clr
  RAM #(.databus("bidir"), .\type ("nonvolatile")) ram_1 (
    .addr(MAR_q), .we(uc1_1_to_ram_s), .oe(uc1_1_to_ram_e), .clk(or_1_out), .data(controlled_buffer_1_out));
  Register MAR (.D(controlled_buffer_1_out), .Q(MAR_q), .clk(uc1_1_to_mar_s));  // open: en, clr
  speaker speaker_1 (
    .in_2(IO_s), .in_3(D_A), .in_4(I_O), .in_1(controlled_buffer_1_out), .out_5(speaker_1_out_5),
    .out_6(speaker_1_out_6), .out_7(speaker_1_out_7));
  // Buzzer #(.vol_width(1)) buzzer_1: pin names not known; wires that end beside it: speaker_1_out_5, speaker_1_out_6, speaker_1_out_7
endmodule

module R (
  input  [7:0] in_1,
  input  in_2,
  input  in_3,
  output [7:0] out_4
);

  wire [7:0] register_1_q;

  Register register_1 (.D(in_1), .Q(register_1_q), .clk(in_2));  // open: en, clr
  assign out_4 = in_3 ? register_1_q : 8'bz;  // Controlled_Buffer controlled_buffer_1
endmodule

module Memory (
  input  [7:0] in_1,
  input  in_2
);

  wire decoder_1_out0, decoder_2_out0;
  wire [7:0] register_1_q;

  Register register_1 (.D(in_1), .Q(register_1_q), .clk(in_2));  // open: en, clr
  Decoder #(.enable("false"), .select(4)) decoder_1 (
    .out0(decoder_1_out0), .sel(register_1_q[7:4]));  // open: out1, out2, out3, out4, out5, out6, out7, out8, out9, out10, out11, out12, out13, out14, out15
  M_cell m_cell_1 ();
  Decoder #(.enable("false"), .select(4)) decoder_2 (
    .out0(decoder_2_out0), .sel(register_1_q[3:0]));  // open: out1, out2, out3, out4, out5, out6, out7, out8, out9, out10, out11, out12, out13, out14, out15
endmodule

module ULA (
  input  [2:0] in_1,
  input  b_1,
  input  c_in,
  input  [7:0] A,
  input  [7:0] B,
  output c_out,
  output [7:0] out_7,
  output a_lager,
  output equal,
  output zero
);

  wire adder_1_cout, and_2_out, left_c_out, rigth_c_out;
  wire [7:0] adder_1_out, and_1_out, left_out_3, not_1_out, or_1_out, rigth_out_3, xor_1_out;

  Adder adder_1 (.a(A), .b(B), .out(adder_1_out), .cin(and_2_out), .cout(adder_1_cout));
  shit_r rigth (.in_2(A), .c_in(and_2_out), .c_out(rigth_c_out), .out_3(rigth_out_3));
  shift_l left (.in_2(A), .c_in(and_2_out), .c_out(left_c_out), .out_3(left_out_3));
  assign not_1_out = ~A;  // NOT_Gate not_1, 8 bits wide
  assign and_1_out = A & B;  // AND_Gate and_1, 8 bits wide
  assign or_1_out = A | B;  // OR_Gate or_1, 8 bits wide
  assign xor_1_out = A ^ B;  // XOR_Gate xor_1, 8 bits wide
  Comparator comparator_1 (.a(A), .b(B), .gt(a_lager), .eq(equal));  // open: lt
  Multiplexer #(.select(3), .width(8)) multiplexer_1 (
    .in0(adder_1_out), .in1(rigth_out_3), .in2(left_out_3), .in3(not_1_out), .in4(and_1_out), .in5(or_1_out),
    .in6(xor_1_out), .in7(A), .out(out_7), .sel(in_1));
  nor nor_1 (zero, out_7[0], out_7[1], out_7[2], out_7[3], out_7[4], out_7[5], out_7[6], out_7[7]);
  and and_2 (and_2_out, ~b_1, c_in);  // AND_Gate
  Multiplexer #(.select(3)) multiplexer_2 (
    .in0(adder_1_cout), .in1(rigth_c_out), .in2(left_c_out), .in3(1'b0), .in4(1'b0), .in5(1'b0), .in6(1'b0),
    .in7(1'b0), .out(c_out), .sel(in_1));
endmodule

module shift_l (
  input  c_in,
  input  [7:0] in_2,
  output [7:0] out_3,
  output c_out
);


  assign c_out = in_2[7];
  assign out_3 = {in_2[6:0], c_in};
endmodule

module shit_r (
  input  c_in,
  input  [7:0] in_2,
  output [7:0] out_3,
  output c_out
);


  assign c_out = in_2[0];
  assign out_3 = {c_in, in_2[7:1]};
endmodule

module clk (
  output clk_s,
  output out_2,
  output clk_e
);

  wire clk_d_out;

  Clock #(.highDuration(2), .lowDuration(2)) clock_1 (.out(out_2));
  Clock #(.highDuration(2), .lowDuration(2), .phaseOffset(3)) clk_d (.out(clk_d_out));
  or or_1 (clk_e, out_2, clk_d_out);
  and and_1 (clk_s, out_2, clk_d_out);
endmodule

module stepper (
  input  in_1,
  output out_2,
  output out_3,
  output out_4,
  output out_5,
  output out_6,
  output out_7,
  output out_8
);

  wire decoder_1_out7;
  wire [2:0] counter_1_q;

  Counter #(.max('h7), .width(3)) counter_1 (
    .D(counter_1_q), .Q(counter_1_q), .clk(in_1), .clr(decoder_1_out7));  // open: load, count, carry, up
  Decoder #(.enable("false"), .select(3)) decoder_1 (
    .out0(out_2), .out1(out_3), .out2(out_4), .out3(out_5), .out4(out_6), .out5(out_7), .out6(out_8),
    .out7(decoder_1_out7), .sel(counter_1_q));
endmodule

module d3x8 (
  input  in_1,
  input  in_2,
  input  in_3,
  input  in_4,
  output out_5,
  output out_6,
  output out_7,
  output out_8,
  output out_9,
  output out_10,
  output out_11,
  output out_12,
  output out_13
);

  wire decoder_1_out0, decoder_1_out1, decoder_1_out2, decoder_1_out3, decoder_1_out4, decoder_1_out5,
       decoder_1_out6, decoder_1_out7, not_1_out;

  not not_1 (not_1_out, in_1);
  Decoder #(.enable("false"), .select(3)) decoder_1 (
    .out0(decoder_1_out0), .out1(decoder_1_out1), .out2(decoder_1_out2), .out3(decoder_1_out3),
    .out4(decoder_1_out4), .out5(decoder_1_out5), .out6(decoder_1_out6), .out7(decoder_1_out7),
    .sel({in_2, in_3, in_4}));
  and and_1 (out_6, not_1_out, decoder_1_out0);
  and and_2 (out_7, not_1_out, decoder_1_out1);
  and and_3 (out_8, not_1_out, decoder_1_out2);
  and and_4 (out_9, not_1_out, decoder_1_out3);
  and and_5 (out_10, not_1_out, decoder_1_out4);
  and and_6 (out_11, not_1_out, decoder_1_out5);
  and and_7 (out_12, not_1_out, decoder_1_out6);
  and and_8 (out_13, not_1_out, decoder_1_out7);

  assign out_5 = in_1;
endmodule

module Ra_Rb_enable (
  input  e,
  input  rb,
  input  ra,
  input  in_4,
  input  in_5,
  input  in_6,
  input  in_7,
  output out_8,
  output out_9,
  output out_10,
  output out_11
);

  wire and_1_out, and_2_out, and_3_out, and_4_out, and_5_out, and_6_out, and_7_out, and_8_out,
       decoder_1_out0, decoder_1_out1, decoder_1_out2, decoder_1_out3, decoder_2_out0, decoder_2_out1,
       decoder_2_out2, decoder_2_out3;

  or or_1 (out_8, and_1_out, and_5_out);
  or or_2 (out_9, and_2_out, and_6_out);
  or or_3 (out_10, and_3_out, and_7_out);
  or or_4 (out_11, and_4_out, and_8_out);
  and and_1 (and_1_out, e, rb, decoder_1_out0);
  and and_2 (and_2_out, e, rb, decoder_1_out1);
  and and_3 (and_3_out, e, rb, decoder_1_out2);
  and and_4 (and_4_out, e, rb, decoder_1_out3);
  and and_5 (and_5_out, e, ra, decoder_2_out0);
  and and_6 (and_6_out, e, ra, decoder_2_out1);
  and and_7 (and_7_out, e, ra, decoder_2_out2);
  and and_8 (and_8_out, e, ra, decoder_2_out3);
  Decoder #(.enable("false"), .select(2)) decoder_1 (
    .out0(decoder_1_out0), .out1(decoder_1_out1), .out2(decoder_1_out2), .out3(decoder_1_out3),
    .sel({in_5, in_4}));
  Decoder #(.enable("false"), .select(2)) decoder_2 (
    .out0(decoder_2_out0), .out1(decoder_2_out1), .out2(decoder_2_out2), .out3(decoder_2_out3),
    .sel({in_7, in_6}));
endmodule

// UC
module UC1 (
  input  from_carry_out,
  input  from_larger,
  input  from_equal,
  input  from_zero,
  input  [7:0] IR_input,
  output to_bus1,
  output to_TMP_s,
  output to_R0_s,
  output to_R0_e,
  output to_R1_s,
  output to_R1_e,
  output to_R2_s,
  output to_R2_e,
  output to_R3_s,
  output to_R3_e,
  output to_MAR_s,
  output to_RAM_s,
  output [2:0] ULA_op,
  output to_RAM_e,
  output init,
  output to_Flags_s,
  output to_ACC_s,
  output to_ACC_e,
  output t0_IAR_s,
  output to_IAR_e,
  output IR_set,
  output Input_Output,
  output Data_Address,
  output to_IO_e,
  output to_IO_s
);

  wire A_out, and_8_out, and_9_out, and_10_out, and_11_out, and_12_out, and_13_out, and_14_out, and_15_out,
       and_16_out, and_17_out, and_18_out, and_19_out, and_20_out, and_21_out, and_22_out, and_23_out,
       and_24_out, and_25_out, and_26_out, and_27_out, C_out, clk_1_out_2, clk_e, clk_s, d3x8_1_out_5,
       d3x8_1_out_6, d3x8_1_out_7, d3x8_1_out_8, d3x8_1_out_9, d3x8_1_out_10, d3x8_1_out_11, d3x8_1_out_12,
       d3x8_1_out_13, E_out, not_1_out, not_2_out, or_2_out, or_3_out, or_4_out, or_5_out, or_6_out,
       or_7_out, or_8_out, or_9_out, or_10_out, or_11_out, or_12_out, s1, s2, s3, s4, s5, s6, Z_out;

  clk clk_1 (.clk_s(clk_s), .out_2(clk_1_out_2), .clk_e(clk_e));
  and and_1 (to_IAR_e, or_2_out, clk_e);
  and and_2 (to_RAM_e, or_3_out, clk_e);
  and and_3 (to_ACC_e, or_4_out, clk_e);
  and and_4 (to_IO_e, and_24_out, clk_e);
  Ra_Rb_enable ra_rb_enable_1 (
    .out_8(to_R0_e), .out_9(to_R1_e), .out_10(to_R2_e), .out_11(to_R3_e), .e(clk_e), .rb(or_5_out),
    .ra(or_6_out), .in_4(IR_input[0]), .in_5(IR_input[1]), .in_6(IR_input[2]), .in_7(IR_input[3]));
  or or_1 (to_bus1, s1, and_16_out, and_15_out, and_12_out);
  or or_2 (or_2_out, s1, and_12_out, and_14_out, and_15_out);
  or or_3 (or_3_out, s2, and_27_out, and_22_out, and_21_out, and_19_out);
  or or_4 (or_4_out, s3, and_23_out, and_26_out, and_25_out);
  or or_5 (or_5_out, and_9_out, and_20_out, and_13_out, and_17_out);
  or or_6 (or_6_out, and_11_out, and_10_out, and_18_out);
  and and_5 (ULA_op[0], s5, IR_input[7], IR_input[4]);
  and and_6 (ULA_op[1], s5, IR_input[7], IR_input[5]);
  and and_7 (ULA_op[2], s5, IR_input[7], IR_input[6]);
  d3x8 d3x8_1 (
    .out_5(d3x8_1_out_5), .in_1(IR_input[7]), .in_2(IR_input[6]), .in_3(IR_input[5]), .in_4(IR_input[4]),
    .out_6(d3x8_1_out_6), .out_7(d3x8_1_out_7), .out_8(d3x8_1_out_8), .out_9(d3x8_1_out_9),
    .out_10(d3x8_1_out_10), .out_11(d3x8_1_out_11), .out_12(d3x8_1_out_12), .out_13(d3x8_1_out_13));
  and and_8 (and_8_out, IR_input[4], IR_input[5], IR_input[6]);
  not not_1 (not_1_out, and_8_out);
  and and_9 (and_9_out, s4, d3x8_1_out_5);
  and and_10 (and_10_out, s4, d3x8_1_out_6);
  and and_11 (and_11_out, s4, d3x8_1_out_7);
  and and_12 (and_12_out, s4, d3x8_1_out_8);
  and and_13 (and_13_out, s4, d3x8_1_out_9);
  and and_14 (and_14_out, s4, d3x8_1_out_10);
  and and_15 (and_15_out, s4, d3x8_1_out_11);
  and and_16 (and_16_out, s4, d3x8_1_out_12);
  and and_17 (and_17_out, s4, d3x8_1_out_13, IR_input[3]);
  stepper stepper_1 (
    .in_1(clk_1_out_2), .out_3(s1), .out_4(s2), .out_5(s3), .out_6(s4), .out_7(s5), .out_8(s6), .out_2(init));
  not not_2 (not_2_out, IR_input[3]);
  and C (C_out, IR_input[3], from_carry_out);
  and A (A_out, IR_input[2], from_larger);
  and E (E_out, IR_input[1], from_equal);
  and Z (Z_out, IR_input[0], from_zero);
  and and_18 (and_18_out, s5, d3x8_1_out_5);
  and and_19 (and_19_out, s5, d3x8_1_out_6);
  and and_20 (and_20_out, s5, d3x8_1_out_7);
  and and_21 (and_21_out, s5, d3x8_1_out_8);
  and and_22 (and_22_out, s5, d3x8_1_out_10);
  and and_23 (and_23_out, s5, d3x8_1_out_11);
  and and_24 (and_24_out, s5, d3x8_1_out_13, not_2_out);
  or or_7 (or_7_out, C_out, A_out, E_out, Z_out);
  and and_25 (and_25_out, s6, d3x8_1_out_5, not_1_out);
  and and_26 (and_26_out, s6, d3x8_1_out_8);
  and and_27 (and_27_out, s6, d3x8_1_out_11, or_7_out);
  or or_8 (or_8_out, s1, and_12_out, and_15_out, and_10_out, and_11_out, and_14_out);
  or or_9 (or_9_out, s3, and_13_out, and_22_out, and_23_out, and_26_out, and_27_out);
  or or_10 (or_10_out, s1, and_12_out, and_15_out, and_18_out);
  or or_11 (or_11_out, and_16_out, and_18_out);
  or or_12 (or_12_out, and_19_out, and_25_out, and_21_out, and_24_out);
  Rb_set rb_set_1 (
    .in_1(or_12_out), .in_2(clk_s), .in_3(IR_input[1]), .in_4(IR_input[0]), .out_5(to_R0_s), .out_6(to_R1_s),
    .out_7(to_R2_s), .out_8(to_R3_s));
  and and_28 (IR_set, clk_s, s2);
  and and_29 (to_MAR_s, clk_s, or_8_out);
  and and_30 (t0_IAR_s, clk_s, or_9_out);
  and and_31 (to_ACC_s, clk_s, or_10_out);
  and and_32 (to_RAM_s, clk_s, and_20_out);
  and and_33 (to_TMP_s, clk_s, and_9_out);
  and and_34 (to_Flags_s, clk_s, or_11_out);
  and and_35 (to_IO_s, clk_s, and_17_out);

  assign Data_Address = IR_input[2];
  assign Input_Output = IR_input[3];

  // Other names for the same wires on the sheet: from_IR[7:0] = IR_input; to_ULA[2:0] = ULA_op
endmodule

module Rb_set (
  input  in_1,
  input  in_2,
  input  in_3,
  input  in_4,
  output out_5,
  output out_6,
  output out_7,
  output out_8
);

  wire decoder_1_out0, decoder_1_out1, decoder_1_out2, decoder_1_out3;

  Decoder #(.enable("false"), .select(2)) decoder_1 (
    .out0(decoder_1_out0), .out1(decoder_1_out1), .out2(decoder_1_out2), .out3(decoder_1_out3),
    .sel({in_3, in_4}));
  and and_1 (out_5, in_2, in_1, decoder_1_out0);
  and and_2 (out_6, in_2, in_1, decoder_1_out1);
  and and_3 (out_7, in_2, in_1, decoder_1_out2);
  and and_4 (out_8, in_2, in_1, decoder_1_out3);
endmodule

module bus1 (
  input  [7:0] in_1,
  input  in_2,
  output [7:0] out_3
);

  Multiplexer #(.width(8)) multiplexer_1 (.in0(in_1), .in1(8'h1), .out(out_3), .sel(in_2));
endmodule

module flag (
  input  in_1,
  input  in_2,
  input  in_3,
  input  in_4,
  input  in_5,
  output out_6,
  output out_7,
  output out_8,
  output out_9
);

  Register #(.width(4)) register_1 (
    .D({in_5, in_3, in_2, in_1}), .Q({out_9, out_8, out_7, out_6}), .clk(in_4));  // open: en, clr
endmodule

module screen (
  input  [7:0] in_1,
  input  in_2,
  input  in_3,
  input  in_4,
  output [6:0] out_5,
  output out_6,
  output out_7
);

  wire and_1_out, comparator_1_eq;

  Comparator comparator_1 (.a(in_1), .b(8'h80), .eq(comparator_1_eq));  // open: gt, lt
  and and_1 (and_1_out, in_2, in_3, in_4);
  and and_2 (out_6, in_2, ~in_3, in_4);  // AND_Gate
  Bit_Extender #(.out_width(7)) bit_extender_1 (.in(in_1), .out(out_5));
  Register #(.width(1)) register_1 (.D(comparator_1_eq), .Q(out_7), .clk(and_1_out));  // open: en, clr
endmodule

module key_adapter (
  input  [7:0] in_1,
  input  in_2,
  input  [6:0] in_3,
  input  in_4,
  input  in_5,
  input  in_6,
  output [7:0] out_7,
  output out_8,
  output out_9
);

  wire and_1_out, comparator_1_eq;
  wire [7:0] bit_extender_1_out, register_2_q;

  and and_1 (and_1_out, in_4, in_5, in_6);
  Comparator comparator_1 (.a(in_1), .b(8'h81), .eq(comparator_1_eq));  // open: gt, lt
  Register #(.width(1)) register_1 (.D(comparator_1_eq), .Q(out_9), .clk(and_1_out));  // open: en, clr
  T_Flip_Flop t_ff_1 (.clk(in_2), .T(1'b1), .Q(out_8));  // open: Qn, preset, reset
  assign bit_extender_1_out = {{1{1'b0}}, in_3};  // Bit_Extender bit_extender_1
  assign out_7 = in_2 ? register_2_q : 8'bz;  // Controlled_Buffer controlled_buffer_1
  Register register_2 (.D(bit_extender_1_out), .Q(register_2_q), .clk(in_2));  // open: en, clr
endmodule

module speaker (
  input  [7:0] in_1,
  input  in_2,
  input  in_3,
  input  in_4,
  output [13:0] out_5,
  output out_6,
  output out_7
);

  wire and_1_out, and_2_out, and_3_out, comparator_1_eq;

  and and_1 (and_1_out, in_2, in_3, in_4);
  Comparator comparator_1 (.a(in_1), .b(8'h82), .eq(comparator_1_eq));  // open: gt, lt
  and and_2 (and_2_out, in_2, ~in_3, in_4);  // AND_Gate
  Register #(.width(1)) register_1 (.D(comparator_1_eq), .Q(out_6), .clk(and_1_out));  // open: en, clr
  Register register_2 (.D(in_1), .Q(out_5[13:6]), .clk(and_3_out));  // open: en, clr
  and and_3 (and_3_out, and_2_out, out_6);

  assign out_5[5:0] = {6{1'b1}};
  assign out_7 = out_6;
endmodule
